// Logisim project W3.circ as structural Verilog
module main (
  input  [3:0] hahaha,
  output a,
  output b,
  output c,
  output d,
  output e,
  output f,
  output g
);

  wire and_1_out, and_2_out, and_3_out, and_4_out, and_5_out, and_6_out, and_7_out, and_8_out, and_9_out,
       and_10_out, and_11_out, and_12_out, and_13_out, and_14_out, and_15_out, and_16_out, and_17_out,
       and_18_out, and_19_out, not_1_out, not_2_out, not_3_out, not_4_out, not_5_out, not_6_out, not_7_out,
       not_8_out, not_9_out, not_10_out, not_11_out, not_12_out, not_13_out, not_14_out, not_15_out,
       not_16_out, not_17_out, not_18_out, not_19_out, not_20_out, not_21_out, not_22_out, not_23_out,
       not_24_out, not_25_out, not_26_out;

  not not_1 (not_1_out, hahaha[2]);
  not not_2 (not_2_out, hahaha[0]);
  not not_3 (not_3_out, hahaha[1]);
  not not_4 (not_4_out, hahaha[0]);
  not not_5 (not_5_out, hahaha[1]);
  not not_6 (not_6_out, hahaha[2]);
  not not_7 (not_7_out, hahaha[0]);
  not not_8 (not_8_out, hahaha[2]);
  not not_9 (not_9_out, hahaha[0]);
  not not_10 (not_10_out, hahaha[1]);
  not not_11 (not_11_out, hahaha[2]);
  not not_12 (not_12_out, hahaha[0]);
  not not_13 (not_13_out, hahaha[3]);
  not not_14 (not_14_out, hahaha[0]);
  not not_15 (not_15_out, hahaha[1]);
  not not_16 (not_16_out, hahaha[0]);
  not not_17 (not_17_out, hahaha[1]);
  not not_18 (not_18_out, hahaha[0]);
  not not_19 (not_19_out, hahaha[1]);
  not not_20 (not_20_out, hahaha[0]);
  not not_21 (not_21_out, hahaha[3]);
  not not_22 (not_22_out, hahaha[2]);
  not not_23 (not_23_out, hahaha[1]);
  not not_24 (not_24_out, hahaha[0]);
  not not_25 (not_25_out, hahaha[1]);
  and and_1 (and_1_out, not_1_out, not_2_out);
  and and_2 (and_2_out, hahaha[2], hahaha[0]);
  not not_26 (not_26_out, hahaha[2]);
  or or_1 (a, and_1_out, hahaha[1], and_2_out, hahaha[3]);
  and and_3 (and_3_out, not_3_out, not_4_out);
  and and_4 (and_4_out, hahaha[1], hahaha[0]);
  or or_2 (c, not_5_out, hahaha[0], hahaha[2]);
  and and_5 (and_5_out, not_6_out, not_7_out);
  and and_6 (and_6_out, not_8_out, hahaha[1]);
  and and_7 (and_7_out, hahaha[1], not_9_out);
  and and_8 (and_8_out, hahaha[2], hahaha[0], not_10_out);
  and and_9 (and_9_out, not_11_out, not_12_out);
  and and_10 (and_10_out, not_13_out, hahaha[1], not_14_out);
  and and_11 (and_11_out, not_15_out, hahaha[3], not_16_out);
  and and_12 (and_12_out, not_17_out, not_18_out);
  and and_13 (and_13_out, hahaha[2], not_19_out);
  and and_14 (and_14_out, hahaha[2], not_20_out);
  and and_15 (and_15_out, not_21_out, not_22_out, hahaha[1]);
  and and_16 (and_16_out, hahaha[2], not_23_out);
  and and_17 (and_17_out, hahaha[2], not_24_out);
  and and_18 (and_18_out, hahaha[3], not_25_out);
  and and_19 (and_19_out, hahaha[3], hahaha[2]);
  or or_3 (b, not_26_out, and_3_out, and_4_out);
  or or_4 (e, and_9_out, and_10_out, and_11_out);
  or or_5 (f, and_12_out, and_13_out, and_14_out, hahaha[3]);
  or or_6 (g, and_15_out, and_16_out, and_17_out, and_18_out, and_19_out);
  or or_7 (d, and_5_out, and_6_out, hahaha[3], and_7_out, and_8_out);
endmodule

module heee (
  input  in_1,
  input  [3:0] in_2,
  input  in_3,
  input  [3:0] in_4
);

  wire and_1_out, clock_1_out, main_1_a, main_1_b, main_1_c, main_1_d, main_1_e, main_1_f, main_1_g,
       main_2_a, main_2_b, main_2_c, main_2_d, main_2_e, main_2_f, main_2_g, or_1_out;
  wire [3:0] counter_1_q, counter_2_q;

  or or_1 (or_1_out, 1'b0, and_1_out);
  Counter #(.max('hf), .ongoal("stay"), .width(4)) counter_1 (
    .clr(in_1), .load(or_1_out), .up(1'b0), .clk(and_1_out), .D(in_2), .Q(counter_1_q));  // open: count, carry
  Counter #(.max('hf), .ongoal("load"), .width(4)) counter_2 (
    .clr(in_3), .load(1'b0), .up(1'b0), .clk(clock_1_out), .D(in_4), .Q(counter_2_q));  // open: count, carry
  Clock clock_1 (.out(clock_1_out));
  and and_1 (and_1_out, counter_2_q[0], counter_2_q[3]);
  main main_1 (
    .hahaha(counter_1_q), .a(main_1_a), .b(main_1_b), .c(main_1_c), .d(main_1_d), .e(main_1_e), .f(main_1_f),
    .g(main_1_g));
  main main_2 (
    .hahaha(counter_2_q), .a(main_2_a), .b(main_2_b), .c(main_2_c), .d(main_2_d), .e(main_2_e), .f(main_2_f),
    .g(main_2_g));
  _7_Segment_Display u_7_segment_display_1 (
    .g(main_1_g), .f(main_1_f), .a(main_1_a), .b(main_1_b), .e(main_1_e), .d(main_1_d), .c(main_1_c));  // open: dp
  _7_Segment_Display u_7_segment_display_2 (
    .g(main_2_g), .f(main_2_f), .a(main_2_a), .b(main_2_b), .e(main_2_e), .d(main_2_d), .c(main_2_c));  // open: dp
endmodule
